// Logisim project SquareRoot_SingleDataPath.circ as structural Verilog: 5 circuits, main circuit Topo
module Topo (
  input  [15:0] valor,
  output ready,
  output [7:0] root
);

  wire clk, controlpath_1_boot, controlpath_1_muxes, controlpath_1_wr_root, controlpath_1_wr_square,
       datapath_1_n, rst;
  wire [1:0] controlpath_1_currentstate, controlpath_1_nextstate;
  wire [9:0] counter_1_q;
  wire [15:0] input_q;

  // Probe on valor
  Clock u_clk (.out(clk));
  Button reset (.out(rst));
  Register #(.width(16)) \input  (.D(valor), .en(controlpath_1_boot), .Q(input_q), .clk(clk), .clr(rst));
  ControlPath controlpath_1 (
    .reset(rst), .clk(clk), .boot(controlpath_1_boot), .wr_root(controlpath_1_wr_root),
    .wr_square(controlpath_1_wr_square), .N(datapath_1_n), .nextState(controlpath_1_nextstate),
    .currentState(controlpath_1_currentstate), .ready(ready), .muxes(controlpath_1_muxes));
  DataPath datapath_1 (
    .valor(input_q), .root_inc(8'h1), .root_init({8{1'b0}}), .square_init(16'h1),
    .wr_root(controlpath_1_wr_root), .boot(controlpath_1_boot), .clk(clk), .reset(rst), .root(root),
    .N(datapath_1_n), .root_sft(5'b00001), .wr_square(controlpath_1_wr_square), .muxes(controlpath_1_muxes));
  // Probe on controlpath_1_currentstate
  // Probe on controlpath_1_nextstate
  // Probe on counter_1_q
  Counter #(.width(10), .max('h3ff)) counter_1 (
    .count(ready), .Q(counter_1_q), .clk(clk), .clr(rst));  // open: load, D, carry
  // Probe on root

  // Notes on the sheet:
  //   root_inc =
  //   root_init =
  //   square_init =
  //   root_sft =
  //   CONFIG
  //   Current State
  //   Next State
  //   ciclos de clock
endmodule

module DataPath (
  input  [15:0] valor,
  input  [15:0] square_init,
  input  [7:0] root_init,
  input  boot,
  input  wr_square,
  input  wr_root,
  input  muxes,
  input  clk,
  input  reset,
  input  [7:0] root_inc,
  input  [4:0] root_sft,
  output N,
  output [7:0] root
);

  wire [7:0] adder_2_out, multiplexer_2_out;
  wire [15:0] adder_1_out;
  wire [16:0] multiplexer_1_out, multiplexer_3_out, multiplexer_4_out, not_1_out, shifter_1_out, square_q;

  // Probe on valor
  Multiplexer #(.width(17)) multiplexer_1 (
    .in0({N, adder_1_out}), .in1({1'b0, square_init}), .out(multiplexer_1_out), .sel(boot));  // open: en
  Multiplexer #(.width(8)) multiplexer_2 (
    .in0(adder_2_out), .in1(root_init), .out(multiplexer_2_out), .sel(boot));  // open: en
  Register #(.width(17)) square (.D(multiplexer_1_out), .en(wr_square), .Q(square_q), .clk(clk), .clr(reset));
  Register u_root (.D(multiplexer_2_out), .en(wr_root), .Q(root), .clk(clk), .clr(reset));
  assign not_1_out = ~square_q;  // NOT_Gate not_1, 17 bits wide
  Shifter #(.width(17)) shifter_1 (.in({{9{1'b0}}, root}), .\dist (root_sft), .out(shifter_1_out));
  Multiplexer #(.width(17)) multiplexer_3 (
    .in0(square_q), .in1(not_1_out), .out(multiplexer_3_out), .sel(muxes));  // open: en
  Multiplexer #(.width(17)) multiplexer_4 (
    .in0(shifter_1_out), .in1({1'b0, valor}), .out(multiplexer_4_out), .sel(muxes));  // open: en
  Adder #(.width(17)) adder_1 (
    .a(multiplexer_3_out), .b(multiplexer_4_out), .out({N, adder_1_out}), .cin(1'b1));  // open: cout
  Adder adder_2 (.a(root), .b(root_inc), .out(adder_2_out));  // open: cin, cout
  // Probe on root

  // Other names for the same wires on the sheet: rst = reset
endmodule

module ControlPath (
  input  N,
  input  reset,
  input  clk,
  output boot,
  output wr_root,
  output wr_square,
  output ready,
  output muxes,
  output [1:0] currentState,
  output [1:0] nextState
);

  NextStage nextstage_1 (.Q1(currentState[1]), .Q0(currentState[0]), .N(N), .q1_2(nextState[1]), .q0_2(nextState[0]));
  D_Flip_Flop Q1 (.clk(clk), .D(nextState[1]), .Q(currentState[1]), .reset(reset));  // open: Qn, preset, en
  D_Flip_Flop Q0 (.clk(clk), .D(nextState[0]), .Q(currentState[0]), .reset(reset));  // open: Qn, preset, en
  Outputs outputs_1 (
    .Q1(currentState[1]), .boot(boot), .Q0(currentState[0]), .wr_root(wr_root), .N(N), .wr_square(wr_square),
    .ready(ready), .muxes(muxes));

  // Notes on the sheet:
  //   NextState Logic
  //   Outputs Logic
endmodule

module NextStage (
  input  Q1,
  input  Q0,
  input  N,
  output q1_2,
  output q0_2
);

  wire and_1_out, and_2_out, not_1_out, not_2_out, not_3_out;

  not not_1 (not_1_out, Q1);
  not not_2 (not_2_out, N);
  not not_3 (not_3_out, Q0);
  and and_1 (and_1_out, not_1_out, Q0, not_2_out);
  and and_2 (and_2_out, Q1, not_3_out);
  or or_1 (q1_2, and_1_out, and_2_out);

  assign q0_2 = 1'b1;
endmodule

module Outputs (
  input  Q1,
  input  Q0,
  input  N,
  output boot,
  output wr_root,
  output wr_square,
  output ready,
  output muxes
);

  wire and_1_out, not_2_out, not_3_out, not_4_out, not_5_out, not_6_out, not_8_out;

  not not_1 (boot, Q0);
  not not_2 (not_2_out, Q1);
  not not_3 (not_3_out, N);
  not not_4 (not_4_out, Q0);
  not not_5 (not_5_out, Q0);
  not not_6 (not_6_out, N);
  not not_7 (muxes, Q1);
  and and_1 (and_1_out, not_2_out, not_3_out);
  not not_8 (not_8_out, Q0);
  or or_1 (wr_square, not_4_out, Q1);
  or or_2 (ready, not_5_out, not_6_out, Q1);
  or or_3 (wr_root, and_1_out, not_8_out);
endmodule
