// Logisim project carries.circ as structural Verilog: 6 circuits, main circuit main
module main (
  input  [17:0] in_1
);

  wire and_1_out, and_2_out, and_3_out, and_4_out, and_5_out, and_6_out, and_7_out, and_8_out, and_9_out,
       nand_1_out, nand_2_out, nor_1_out, nor_2_out, nor_3_out, nor_4_out, nor_5_out, nor_6_out, nor_7_out;
  wire [17:0] not_1_out;

  assign not_1_out = ~in_1;  // NOT_Gate not_1, 18 bits wide
  and and_1 (and_1_out, in_1[0], in_1[1], in_1[2]);
  and and_2 (and_2_out, in_1[3], in_1[4], in_1[5]);
  and and_3 (and_3_out, in_1[6], in_1[7], in_1[8]);
  and and_4 (and_4_out, in_1[9], in_1[10], in_1[11]);
  and and_5 (and_5_out, in_1[12], in_1[13], in_1[14]);
  and and_6 (and_6_out, in_1[15], in_1[16], in_1[17]);
  nor nor_1 (nor_1_out, not_1_out[0], not_1_out[1], not_1_out[2]);
  nor nor_2 (nor_2_out, not_1_out[3], not_1_out[4], not_1_out[5]);
  nor nor_3 (nor_3_out, not_1_out[6], not_1_out[7], not_1_out[8]);
  nor nor_4 (nor_4_out, not_1_out[9], not_1_out[10], not_1_out[11]);
  nor nor_5 (nor_5_out, not_1_out[12], not_1_out[13], not_1_out[14]);
  nor nor_6 (nor_6_out, not_1_out[15], not_1_out[16], not_1_out[17]);
  and and_7 (and_7_out, and_1_out, and_2_out, and_3_out);
  and and_8 (and_8_out, and_7_out, and_9_out);
  and and_9 (and_9_out, and_4_out, and_5_out, and_6_out);
  nand nand_1 (nand_1_out, nor_1_out, nor_2_out, nor_3_out);
  nand nand_2 (nand_2_out, nor_4_out, nor_5_out, nor_6_out);
  nor nor_7 (nor_7_out, nand_1_out, nand_2_out);
endmodule

module carry4 (
  input  [14:0] in_1
);

  wire and_1_out, and_2_out, and_3_out, and_4_out, and_5_out, and_6_out, nand_1_out, nand_2_out, nor_1_out,
       nor_2_out, nor_3_out, nor_4_out, nor_5_out, nor_6_out, nor_7_out, or_1_out, or_2_out, or_3_out;

  and and_1 (and_1_out, in_1[0], in_1[1], in_1[2]);
  and and_2 (and_2_out, and_1_out, and_3_out);
  and and_3 (and_3_out, in_1[3], in_1[4]);
  and and_4 (and_4_out, in_1[5], in_1[6], in_1[7], in_1[8]);
  and and_5 (and_5_out, in_1[9], in_1[10], in_1[11]);
  and and_6 (and_6_out, in_1[12], in_1[13]);
  nor nor_1 (nor_1_out, ~in_1[0], ~in_1[1], ~in_1[2]);  // NOR_Gate
  nor nor_2 (nor_2_out, ~in_1[3], ~in_1[4]);  // NOR_Gate
  nor nor_3 (nor_3_out, ~in_1[5], ~in_1[6], ~in_1[7], ~in_1[8]);  // NOR_Gate
  nor nor_4 (nor_4_out, ~in_1[9], ~in_1[10], ~in_1[11]);  // NOR_Gate
  nor nor_5 (nor_5_out, ~in_1[12], ~in_1[13]);  // NOR_Gate
  or or_1 (or_1_out, and_4_out, and_5_out);
  or or_2 (or_2_out, and_6_out, in_1[14]);
  nand nand_1 (nand_1_out, nor_1_out, nor_2_out);
  nor nor_6 (nor_6_out, nor_3_out, nor_4_out);
  nor nor_7 (nor_7_out, nor_5_out, in_1[14]);
  or or_3 (or_3_out, and_2_out, or_1_out, or_2_out);
  nand nand_2 (nand_2_out, nand_1_out, nor_6_out, nor_7_out);
endmodule

module carry5 (
  input  [10:0] in_1
);

  wire and_1_out, and_2_out, and_3_out, and_4_out, and_5_out, and_6_out, and_7_out, and_8_out, and_9_out,
       nand_1_out, nand_2_out, nor_1_out, nor_2_out, nor_3_out, nor_4_out, nor_5_out, nor_6_out, nor_7_out,
       nor_8_out, or_1_out, or_2_out, undriven;

  and and_1 (and_1_out, in_1[0], in_1[1], in_1[2]);
  and and_2 (and_2_out, and_1_out, and_3_out);
  and and_3 (and_3_out, in_1[3], in_1[4], in_1[5]);
  and and_4 (and_4_out, in_1[0], in_1[1], in_1[2]);
  and and_5 (and_5_out, and_4_out, and_6_out);
  and and_6 (and_6_out, in_1[3], in_1[6]);
  and and_7 (and_7_out, in_1[0], in_1[1], in_1[2], in_1[7]);
  and and_8 (and_8_out, in_1[0], in_1[1], in_1[8]);
  and and_9 (and_9_out, in_1[0], in_1[9]);
  // NOR_Gate nor_1 has open pins: out=nor_1_out
  // NOR_Gate nor_2 has open pins: out=nor_2_out
  // NOR_Gate nor_3 has open pins: out=nor_3_out
  // NOR_Gate nor_4 has open pins: out=nor_4_out
  // NOR_Gate nor_5 has open pins: out=nor_5_out
  // NOR_Gate nor_6 has open pins: out=nor_6_out
  // NOR_Gate nor_7 has open pins: out=nor_7_out
  or or_1 (or_1_out, and_7_out, and_8_out, and_9_out, in_1[10]);
  or or_2 (or_2_out, and_2_out, and_5_out, or_1_out);
  nand nand_1 (nand_1_out, nor_1_out, nor_2_out);
  nand nand_2 (nand_2_out, nor_3_out, nor_4_out);
  // NAND_Gate nand_3 has open pins: in0=nand_1_out, in1=nand_2_out, in2=nor_8_out, out=open
  nor nor_8 (nor_8_out, nor_5_out, nor_6_out, nor_7_out, undriven);
endmodule

module carry6 (
  input  [10:0] in_1
);

  wire and_1_p5, and_2_out, and_3_p5, and_4_out, and_5_out, and_6_out, and_7_out, and_8_out, and_9_out,
       and_10_out, and_11_out, and_12_out, nand_1_out, nand_2_out, nand_3_out, nand_4_out, nor_1_out,
       nor_2_out, nor_3_out, nor_4_out, nor_5_out, nor_6_out, nor_7_out, nor_8_out, nor_9_out, nor_10_out,
       or_1_out, or_2_out, undriven, undriven_2;

  // AND_Gate and_1: pin names not known; wires that end beside it: in_1[0], in_1[1], in_1[2], in_1[3], and_1_p5
  and and_2 (and_2_out, and_1_p5, and_3_p5);
  // AND_Gate and_3: pin names not known; wires that end beside it: in_1[0], in_1[1], in_1[2], in_1[3], and_3_p5
  // AND_Gate and_4 has open pins: out=and_4_out
  and and_5 (and_5_out, and_4_out, and_6_out);
  // AND_Gate and_6 has open pins: out=and_6_out
  // AND_Gate and_7 has open pins: out=and_7_out
  and and_8 (and_8_out, and_7_out, and_9_out);
  // AND_Gate and_9 has open pins: out=and_9_out
  // AND_Gate and_10 has open pins: out=and_10_out
  or or_1 (or_1_out, and_10_out, and_11_out, and_12_out, undriven);
  // AND_Gate and_11 has open pins: out=and_11_out
  // AND_Gate and_12 has open pins: out=and_12_out
  // NOR_Gate nor_1 has open pins: out=nor_1_out
  nand nand_1 (nand_1_out, nor_1_out, nor_2_out);
  // NOR_Gate nor_2 has open pins: out=nor_2_out
  // NOR_Gate nor_3 has open pins: out=nor_3_out
  nand nand_2 (nand_2_out, nor_3_out, nor_4_out);
  // NOR_Gate nor_4 has open pins: out=nor_4_out
  // NOR_Gate nor_5 has open pins: out=nor_5_out
  nand nand_3 (nand_3_out, nor_5_out, nor_6_out);
  // NOR_Gate nor_6 has open pins: out=nor_6_out
  // NOR_Gate nor_7 has open pins: out=nor_7_out
  // NOR_Gate nor_8 has open pins: out=nor_8_out
  // NOR_Gate nor_9 has open pins: out=nor_9_out
  or or_2 (or_2_out, and_2_out, and_5_out, and_8_out, or_1_out);
  nand nand_4 (nand_4_out, nand_1_out, nand_2_out, nand_3_out, nor_10_out);
  nor nor_10 (nor_10_out, nor_7_out, nor_8_out, nor_9_out, undriven_2);
endmodule

module carry7 (
);

  wire and_1_out, and_2_out, and_3_out, and_4_out, and_5_out, and_6_out, and_7_out, and_8_out, and_9_out,
       and_10_out, and_11_out, and_12_out, and_13_out, and_14_out, and_15_out, nand_1_out, nand_2_out,
       nand_3_out, nand_4_out, nand_5_out, nand_6_out, nand_7_out, nand_8_out, nand_9_out, nand_10_out,
       nand_11_out, nor_1_out, nor_2_out, nor_3_out, nor_4_out, nor_5_out, nor_6_out, not_1_out, or_1_out,
       or_2_out, or_3_out, undriven, undriven_2;

  // AND_Gate and_1 has open pins: out=and_1_out
  and and_2 (and_2_out, and_1_out, and_3_out);
  // AND_Gate and_3 has open pins: out=and_3_out
  // AND_Gate and_4 has open pins: out=and_4_out
  and and_5 (and_5_out, and_4_out, and_6_out);
  // AND_Gate and_6 has open pins: out=and_6_out
  // AND_Gate and_7 has open pins: out=and_7_out
  and and_8 (and_8_out, and_7_out, and_9_out);
  // AND_Gate and_9 has open pins: out=and_9_out
  // AND_Gate and_10 has open pins: out=and_10_out
  and and_11 (and_11_out, and_10_out, and_12_out);
  // AND_Gate and_12 has open pins: out=and_12_out
  // AND_Gate and_13 has open pins: out=and_13_out
  // AND_Gate and_14 has open pins: out=and_14_out
  // AND_Gate and_15 has open pins: out=and_15_out
  or or_1 (or_1_out, and_2_out, and_5_out, and_8_out);
  or or_2 (or_2_out, and_11_out, and_13_out, or_3_out);
  or or_3 (or_3_out, and_14_out, and_15_out, undriven);
  // OR_Gate or_4 has open pins: in0=or_1_out, in1=or_2_out, out=open
  // NAND_Gate nand_1 has open pins: out=nand_1_out
  // NAND_Gate nand_2 has open pins: out=nand_2_out
  // NAND_Gate nand_3 has open pins: out=nand_3_out
  // NAND_Gate nand_4 has open pins: out=nand_4_out
  // NAND_Gate nand_5 has open pins: out=nand_5_out
  // NAND_Gate nand_6 has open pins: out=nand_6_out
  // NAND_Gate nand_7 has open pins: out=nand_7_out
  // NOT_Gate not_1 has open pins: in=open, out=not_1_out
  // NAND_Gate nand_8 has open pins: out=nand_8_out
  // NAND_Gate nand_9 has open pins: out=nand_9_out
  // NAND_Gate nand_10 has open pins: out=nand_10_out
  nor nor_1 (nor_1_out, nand_1_out, nand_2_out);
  nor nor_2 (nor_2_out, nand_3_out, nand_4_out);
  nor nor_3 (nor_3_out, nand_5_out, nand_6_out);
  nor nor_4 (nor_4_out, nand_7_out, not_1_out);
  nand nand_11 (nand_11_out, nand_8_out, nand_9_out, nand_10_out);
  nor nor_5 (nor_5_out, nor_1_out, nor_2_out, nor_3_out);
  nor nor_6 (nor_6_out, nor_4_out, nand_11_out, undriven_2);
  // NAND_Gate nand_12 has open pins: in0=nor_5_out, in1=nor_6_out, out=open
endmodule

module carry8 (
);

  wire and_1_out, and_2_out, and_3_out, and_4_out, and_5_out, and_6_out, and_7_out, and_8_out, and_9_out,
       and_10_out, and_11_out, and_12_out, and_13_out, and_14_out, and_15_out, nand_1_out, nand_2_out,
       nand_3_out, nand_4_out, nand_5_out, nand_6_out, nand_7_out, nand_8_out, nand_9_out, nand_10_out,
       nand_11_out, nor_1_out, nor_2_out, nor_3_out, nor_4_out, nor_5_out, nor_6_out, nor_7_out, nor_8_out,
       not_1_out, or_1_out, or_2_out, or_3_out, or_4_out, undriven, undriven_2, undriven_3;

  // AND_Gate and_1 has open pins: out=and_1_out
  // AND_Gate and_2 has open pins: out=and_2_out
  // AND_Gate and_3 has open pins: out=and_3_out
  // AND_Gate and_4 has open pins: out=and_4_out
  // AND_Gate and_5 has open pins: out=and_5_out
  // AND_Gate and_6 has open pins: out=and_6_out
  // AND_Gate and_7 has open pins: out=and_7_out
  // AND_Gate and_8 has open pins: out=and_8_out
  // AND_Gate and_9 has open pins: out=and_9_out
  // AND_Gate and_10 has open pins: out=and_10_out
  and and_11 (and_11_out, and_1_out, and_2_out, and_3_out);
  and and_12 (and_12_out, and_1_out, and_2_out, undriven);
  and and_13 (and_13_out, and_1_out, and_4_out);
  and and_14 (and_14_out, and_5_out, and_6_out);
  and and_15 (and_15_out, and_5_out, and_7_out);
  or or_1 (or_1_out, and_11_out, and_12_out, and_13_out);
  or or_2 (or_2_out, and_14_out, and_15_out, and_8_out);
  or or_3 (or_3_out, and_9_out, and_10_out, undriven_2);
  or or_4 (or_4_out, or_1_out, or_2_out, or_3_out);
  // NAND_Gate nand_1 has open pins: out=nand_1_out
  // NAND_Gate nand_2 has open pins: out=nand_2_out
  // NAND_Gate nand_3 has open pins: out=nand_3_out
  // NOT_Gate not_1 has open pins: in=open, out=not_1_out
  // NAND_Gate nand_4 has open pins: out=nand_4_out
  // NAND_Gate nand_5 has open pins: out=nand_5_out
  // NAND_Gate nand_6 has open pins: out=nand_6_out
  // NAND_Gate nand_7 has open pins: out=nand_7_out
  // NAND_Gate nand_8 has open pins: out=nand_8_out
  // NAND_Gate nand_9 has open pins: out=nand_9_out
  // NAND_Gate nand_10 has open pins: out=nand_10_out
  nor nor_1 (nor_1_out, nand_1_out, nand_2_out, nand_3_out);
  nor nor_2 (nor_2_out, nand_1_out, nand_2_out, not_1_out);
  nor nor_3 (nor_3_out, nand_1_out, nand_4_out);
  nor nor_4 (nor_4_out, nand_5_out, nand_6_out);
  nor nor_5 (nor_5_out, nand_5_out, nand_7_out);
  nor nor_6 (nor_6_out, nor_1_out, nor_2_out, nor_3_out);
  nor nor_7 (nor_7_out, nor_4_out, nor_5_out, nand_8_out);
  nor nor_8 (nor_8_out, nand_9_out, nand_10_out, undriven_3);
  nand nand_11 (nand_11_out, nor_6_out, nor_7_out, nor_8_out);
endmodule
