// Logisim project SquareRoot_DualDataPath.circ as structural Verilog: 5 circuits, main circuit Topo
module Topo (
  input  [15:0] valor,
  output ready,
  output [7:0] root
);

  wire clk, controlpath_1_boot, controlpath_1_muxes, controlpath_1_root, controlpath_1_wr_mux_root,
       controlpath_1_wr_root, controlpath_1_wr_square, datapath_1_n, datapath_2_n, register_1_q, rst;
  wire [1:0] controlpath_1_currentstate, controlpath_1_nextstate;
  wire [7:0] datapath_1_root, datapath_2_root;
  wire [9:0] counter_1_q;
  wire [15:0] input_q;

  // Probe on valor
  Clock u_clk (.out(clk));
  Button reset (.out(rst));
  Register #(.width(16)) \input  (.D(valor), .en(controlpath_1_boot), .Q(input_q), .clk(clk), .clr(rst));
  ControlPath controlpath_1 (
    .reset(rst), .clk(clk), .boot(controlpath_1_boot), .wr_root(controlpath_1_wr_root),
    .wr_square(controlpath_1_wr_square), .N1(datapath_1_n), .nextState(controlpath_1_nextstate),
    .currentState(controlpath_1_currentstate), .ready(ready), .muxes(controlpath_1_muxes), .N2(datapath_2_n),
    .root(controlpath_1_root), .wr_mux_root(controlpath_1_wr_mux_root));
  DataPath datapath_1 (
    .valor(input_q), .root_inc(8'h2), .root_init({8{1'b0}}), .square_init(16'h1),
    .wr_root(controlpath_1_wr_root), .boot(controlpath_1_boot), .clk(clk), .reset(rst),
    .root(datapath_1_root), .N(datapath_1_n), .root_sft(5'b00010), .wr_square(controlpath_1_wr_square),
    .muxes(controlpath_1_muxes));
  DataPath datapath_2 (
    .valor(input_q), .root_inc(8'h2), .root_init(8'h1), .square_init(16'h4), .wr_root(controlpath_1_wr_root),
    .boot(controlpath_1_boot), .clk(clk), .reset(rst), .root(datapath_2_root), .N(datapath_2_n),
    .root_sft(5'b00010), .wr_square(controlpath_1_wr_square), .muxes(controlpath_1_muxes));
  Register #(.width(1)) register_1 (
    .D(controlpath_1_root), .en(controlpath_1_wr_mux_root), .Q(register_1_q), .clk(clk), .clr(rst));
  Multiplexer #(.width(8)) multiplexer_1 (
    .in0(datapath_1_root), .in1(datapath_2_root), .out(root), .sel(register_1_q));  // open: en
  // Probe on controlpath_1_currentstate
  // Probe on controlpath_1_nextstate
  Counter #(.width(10), .max('h3ff)) counter_1 (
    .count(ready), .Q(counter_1_q), .clk(clk), .clr(rst));  // open: load, D, carry
  // Probe on counter_1_q
  // Probe on root

  // Notes on the sheet:
  //   CONFIG
  //   root_inc =
  //   root_sft =
  //   DP1
  //   root_init1 =
  //   square_init1 =
  //   DP2
  //   root_init2 =
  //   square_init2 =
  //   DP1
  //   DP2
  //   Current State
  //   Next State
  //   ciclos de clock
endmodule

module DataPath (
  input  [15:0] valor,
  input  [15:0] square_init,
  input  [7:0] root_init,
  input  boot,
  input  wr_square,
  input  wr_root,
  input  muxes,
  input  clk,
  input  reset,
  input  [7:0] root_inc,
  input  [4:0] root_sft,
  output N,
  output [7:0] root
);

  wire [7:0] adder_2_out, multiplexer_2_out;
  wire [15:0] adder_1_out;
  wire [16:0] multiplexer_1_out, multiplexer_3_out, multiplexer_4_out, not_1_out, shifter_1_out, square_q;

  // Probe on valor
  Multiplexer #(.width(17)) multiplexer_1 (
    .in0({N, adder_1_out}), .in1({1'b0, square_init}), .out(multiplexer_1_out), .sel(boot));  // open: en
  Multiplexer #(.width(8)) multiplexer_2 (
    .in0(adder_2_out), .in1(root_init), .out(multiplexer_2_out), .sel(boot));  // open: en
  Register #(.width(17)) square (.D(multiplexer_1_out), .en(wr_square), .Q(square_q), .clk(clk), .clr(reset));
  // Probe on square_q
  Register u_root (.D(multiplexer_2_out), .en(wr_root), .Q(root), .clk(clk), .clr(reset));
  assign not_1_out = ~square_q;  // NOT_Gate not_1, 17 bits wide
  Shifter #(.width(17)) shifter_1 (.in({{9{1'b0}}, root}), .\dist (root_sft), .out(shifter_1_out));
  Multiplexer #(.width(17)) multiplexer_3 (
    .in0(square_q), .in1(not_1_out), .out(multiplexer_3_out), .sel(muxes));  // open: en
  Multiplexer #(.width(17)) multiplexer_4 (
    .in0(shifter_1_out), .in1({1'b0, valor}), .out(multiplexer_4_out), .sel(muxes));  // open: en
  Adder #(.width(17)) adder_1 (
    .a(multiplexer_3_out), .b(multiplexer_4_out), .out({N, adder_1_out}), .cin(muxes));  // open: cout
  Adder adder_2 (.a(root), .b(root_inc), .out(adder_2_out));  // open: cin, cout
  // Probe on root

  // Other names for the same wires on the sheet: rst = reset
endmodule

module ControlPath (
  input  N2,
  input  N1,
  input  reset,
  input  clk,
  output boot,
  output wr_root,
  output wr_square,
  output ready,
  output muxes,
  output root,
  output wr_mux_root,
  output [1:0] currentState,
  output [1:0] nextState
);

  NextStage nextstage_1 (
    .Q1(currentState[1]), .Q0(currentState[0]), .N2(N2), .N1(N1), .q1_2(nextState[1]), .q0_2(nextState[0]));
  D_Flip_Flop Q1 (.clk(clk), .D(nextState[1]), .Q(currentState[1]), .reset(reset));  // open: Qn, preset, en
  D_Flip_Flop Q0 (.clk(clk), .D(nextState[0]), .Q(currentState[0]), .reset(reset));  // open: Qn, preset, en
  Outputs outputs_1 (
    .Q1(currentState[1]), .boot(boot), .Q0(currentState[0]), .wr_root(wr_root), .N2(N2), .N1(N1),
    .wr_square(wr_square), .ready(ready), .muxes(muxes), .root(root), .mr_mux_root(wr_mux_root));

  // Notes on the sheet:
  //   NextState Logic
  //   Outputs Logic
endmodule

module NextStage (
  input  Q1,
  input  Q0,
  input  N2,
  input  N1,
  output q1_2,
  output q0_2
);

  wire and_1_out, and_2_out, and_3_out, and_4_out, and_5_out, not_1_out, not_2_out, not_3_out, not_4_out,
       not_5_out, not_6_out, not_7_out;

  not not_1 (not_1_out, Q1);
  and and_1 (and_1_out, not_1_out, Q0);
  and and_2 (and_2_out, Q1, not_2_out);
  not not_2 (not_2_out, Q0);
  not not_3 (not_3_out, Q1);
  and and_3 (and_3_out, not_3_out, not_4_out);
  not not_4 (not_4_out, Q0);
  not not_5 (not_5_out, Q1);
  not not_6 (not_6_out, N2);
  and and_4 (and_4_out, not_5_out, not_6_out, not_7_out);
  not not_7 (not_7_out, N1);
  and and_5 (and_5_out, Q1, Q0);
  or or_1 (q1_2, and_1_out, and_2_out);
  or or_2 (q0_2, and_3_out, and_4_out, and_5_out);
endmodule

module Outputs (
  input  Q1,
  input  Q0,
  input  N2,
  input  N1,
  output boot,
  output wr_root,
  output wr_square,
  output ready,
  output muxes,
  output root,
  output mr_mux_root
);

  wire and_2_out, and_3_out, and_4_out, and_5_out, and_6_out, and_7_out, not_1_out, not_2_out, not_3_out,
       not_4_out, not_5_out, not_6_out, not_7_out, not_8_out, not_9_out, not_10_out, not_13_out, not_14_out;

  not not_1 (not_1_out, Q1);
  and and_1 (boot, not_1_out, not_2_out);
  not not_2 (not_2_out, Q0);
  not not_3 (not_3_out, Q1);
  and and_2 (and_2_out, not_3_out, not_4_out);
  not not_4 (not_4_out, Q0);
  not not_5 (not_5_out, Q1);
  not not_6 (not_6_out, N2);
  and and_3 (and_3_out, not_5_out, not_6_out, not_7_out);
  not not_7 (not_7_out, N1);
  not not_8 (not_8_out, Q1);
  and and_4 (and_4_out, not_8_out, not_9_out);
  not not_9 (not_9_out, Q0);
  and and_5 (and_5_out, Q1, Q0);
  not not_10 (not_10_out, Q1);
  or or_1 (ready, not_10_out, Q0);
  not not_11 (muxes, Q1);
  not not_12 (root, N1);
  not not_13 (not_13_out, Q1);
  and and_6 (and_6_out, not_13_out, Q0, N1);
  not not_14 (not_14_out, Q1);
  and and_7 (and_7_out, not_14_out, Q0, N2);
  or or_2 (wr_root, and_2_out, and_3_out);
  or or_3 (wr_square, and_4_out, and_5_out);
  or or_4 (mr_mux_root, and_6_out, and_7_out);
endmodule
