// Logisim project SquareRoot_Pipeline_V2.12.circ as structural Verilog: 7 circuits, main circuit Pipeline
module Pipeline (
  input  [15:0] \input ,
  output ready,
  output [7:0] root
);

  wire adder_1_cout, clk, comparator_1_lt, controlpath_1_en_pipe, controlpath_1_wr_input, not_1_out, rst,
       stage2_1_co_o;
  wire [7:0] adder_2_out, stage2_1_a_high_o, stage2_1_b_high_o;
  wire [7:4] stage2_1_n2_o;
  wire [8:0] adder_1_out;
  wire [9:0] counter_1_q;
  wire [15:0] stage1_1_input_o;
  wire [16:0] stage1_1_square1_o, stage2_1_sum_low_o;

  Clock clock (.out(clk));
  Button reset (.out(rst));
  // Probe on \input 
  ControlPath controlpath_1 (
    .N(stage2_1_n2_o[7]), .clk(clk), .rst(rst), .en_pipe(controlpath_1_en_pipe),
    .wr_input(controlpath_1_wr_input));
  STAGE1 stage1_1 (
    .root(adder_2_out), .input_o(stage1_1_input_o), .root_o(root), .en_pipe(controlpath_1_en_pipe),
    .wr_input(controlpath_1_wr_input), .clk(clk), .rst(rst), .square1(stage2_1_sum_low_o),
    .square1_o(stage1_1_square1_o), .\input (\input ), .wr_root(ready));
  not not_1 (not_1_out, stage2_1_n2_o[7]);
  Comparator #(.width(17), .mode("unsigned")) comparator_1 (
    .a({1'b0, stage1_1_input_o}), .b(stage1_1_square1_o), .lt(comparator_1_lt));  // open: gt, eq
  Adder #(.width(9)) adder_1 (
    .a(stage1_1_square1_o[8:0]), .b({root[6:0], 2'b00}), .out(adder_1_out), .cout(adder_1_cout));  // open: cin
  Adder adder_2 (
    .a({{3{stage2_1_n2_o[7]}}, {3{stage2_1_n2_o[4]}}, 2'b01}), .b(root), .out(adder_2_out));  // open: cin, cout
  STAGE2 stage2_1 (
    .ready(not_1_out), .Sum_low(adder_1_out), .Co(adder_1_cout), .A_high(stage1_1_square1_o[16:9]),
    .B_high({{7{1'b0}}, root[7]}), .ready_o(ready), .Sum_low_o(stage2_1_sum_low_o[8:0]),
    .Co_o(stage2_1_co_o), .A_high_o(stage2_1_a_high_o), .B_high_o(stage2_1_b_high_o),
    .en_pipe(controlpath_1_en_pipe), .clk(clk), .rst(rst), .N2(comparator_1_lt), .N2_o(stage2_1_n2_o[4]),
    .N1(comparator_1_lt), .N1_o(stage2_1_n2_o[7]));
  Adder adder_3 (
    .a(stage2_1_a_high_o), .b(stage2_1_b_high_o), .out(stage2_1_sum_low_o[16:9]), .cin(stage2_1_co_o));  // open: cout
  // Probe on counter_1_q
  Counter #(.width(10), .max('h3ff)) counter_1 (
    .count(ready), .Q(counter_1_q), .clk(clk), .clr(rst));  // open: load, D, carry
  // Probe on root

  // Notes on the sheet:
  //   root<<2 + 3
  //   1 or -3
  //   cicles
endmodule

module STAGE1 (
  input  wr_root,
  input  [15:0] \input ,
  input  [16:0] square1,
  input  [7:0] root,
  input  en_pipe,
  input  wr_input,
  input  clk,
  input  rst,
  output [15:0] input_o,
  output [16:0] square1_o,
  output [7:0] root_o
);

  Register #(.width(16)) u_input (.D(\input ), .en(wr_input), .Q(input_o), .clk(clk), .clr(rst));
  Register #(.width(17)) u_square1 (.D(square1), .en(en_pipe), .Q(square1_o), .clk(clk), .clr(rst));
  Register u_root (.D(root), .en(wr_root), .Q(root_o), .clk(clk), .clr(rst));
endmodule

module STAGE2 (
  input  ready,
  input  N1,
  input  N2,
  input  [8:0] Sum_low,
  input  Co,
  input  [7:0] A_high,
  input  [7:0] B_high,
  input  en_pipe,
  input  clk,
  input  rst,
  output ready_o,
  output N1_o,
  output N2_o,
  output [8:0] Sum_low_o,
  output Co_o,
  output [7:0] A_high_o,
  output [7:0] B_high_o
);

  D_Flip_Flop d_ff_1 (.clk(clk), .D(ready), .Q(ready_o), .preset(rst), .en(en_pipe));  // open: Qn, reset
  Register #(.width(1)) N (.D(N1), .en(en_pipe), .Q(N1_o), .clk(clk), .clr(rst));
  Register #(.width(1)) N_2 (.D(N2), .en(en_pipe), .Q(N2_o), .clk(clk), .clr(rst));
  reg_sum_low reg_sum_low_1 (.D(Sum_low), .En(en_pipe), .out_5(Sum_low_o), .Clk(clk), .Reset(rst));
  Register #(.width(1)) u_Co (.D(Co), .en(en_pipe), .Q(Co_o), .clk(clk), .clr(rst));
  Register u_A_high (.D(A_high), .en(en_pipe), .Q(A_high_o), .clk(clk), .clr(rst));
  Register u_B_high (.D(B_high), .en(en_pipe), .Q(B_high_o), .clk(clk), .clr(rst));
endmodule

module ControlPath (
  input  N,
  input  clk,
  input  rst,
  output wr_input,
  output en_pipe
);

  wire nextstage_1_q0_2, nextstage_1_q1_2, Q0_q, Q1_q;

  NextStage nextstage_1 (.Q1(Q1_q), .Q0(Q0_q), .N(N), .q1_2(nextstage_1_q1_2), .q0_2(nextstage_1_q0_2));
  D_Flip_Flop Q1 (.clk(clk), .D(nextstage_1_q1_2), .Q(Q1_q), .reset(rst));  // open: Qn, preset, en
  D_Flip_Flop Q0 (.clk(clk), .D(nextstage_1_q0_2), .Q(Q0_q), .reset(rst));  // open: Qn, preset, en
  Outputs outputs_1 (.Q1(Q1_q), .Q0(Q0_q), .wr_input(wr_input), .en_pipe(en_pipe));
endmodule

module NextStage (
  input  Q1,
  input  Q0,
  input  N,
  output q1_2,
  output q0_2
);

  wire and_1_out;

  and and_1 (and_1_out, Q0, N);
  or or_1 (q1_2, and_1_out, Q1);

  assign q0_2 = 1'b1;
endmodule

module Outputs (
  input  Q1,
  input  Q0,
  output wr_input,
  output en_pipe
);

  wire not_2_out;

  not not_1 (wr_input, Q0);
  not not_2 (not_2_out, Q1);
  and and_1 (en_pipe, not_2_out, Q0);
endmodule

module reg_sum_low (
  input  [8:0] D,
  input  En,
  input  Clk,
  input  Reset,
  output [8:0] out_5
);

  D_Flip_Flop d_ff_1 (.clk(Clk), .D(D[0]), .Q(out_5[0]), .preset(Reset), .en(En));  // open: Qn, reset
  Register register_1 (.D(D[8:1]), .en(En), .Q(out_5[8:1]), .clk(Clk), .clr(Reset));
endmodule
