// Logisim project SquareRoot_Pipeline_V2.2.circ as structural Verilog: 14 circuits, main circuit Pipeline
module Pipeline (
  input  [15:0] \input ,
  output ready,
  output [7:0] root
);

  wire adder_1_cout, adder_2_cout, adder_3_cout, adder_5_cout, clk, comparator_1_lt, controlpath_1_en_pipe,
       controlpath_1_ready, controlpath_1_wr_input, rst, stage2_1_co_o, stage2_1_co_root_o, stage2_1_n_o,
       stage3_1_co_o, stage4_1_co_o;
  wire [3:0] adder_2_out, adder_3_out, adder_5_out, adder_6_out, stage2_1_root_high_o, stage4_1_a_high_o,
       stage4_1_b_high_o;
  wire [3:1] not_1_out;
  wire [4:0] adder_1_out, stage2_1_square_sum_o;
  wire [7:0] stage2_1_root_sum_o, stage3_1_a_high_o, stage3_1_b_high_o;
  wire [8:0] stage3_1_square_sum_o;
  wire [9:0] counter_1_q;
  wire [11:0] stage2_1_a_high_o, stage2_1_b_high_o;
  wire [12:0] stage4_1_square_sum_o;
  wire [15:0] stage1_1_input_o;
  wire [16:0] stage1_1_square1_o;

  Clock clock (.out(clk));
  Button reset (.out(rst));
  // Probe on \input 
  ControlPath controlpath_1 (
    .N(stage2_1_n_o), .clk(clk), .rst(rst), .en_pipe(controlpath_1_en_pipe),
    .wr_input(controlpath_1_wr_input), .ready(controlpath_1_ready), .mux_root(not_1_out[3]));
  STAGE1 stage1_1 (
    .root(stage2_1_root_sum_o), .input_o(stage1_1_input_o), .root_o(root), .en_pipe(controlpath_1_en_pipe),
    .wr_input(controlpath_1_wr_input), .clk(clk), .rst(rst), .square1({adder_6_out, stage4_1_square_sum_o}),
    .square1_o(stage1_1_square1_o), .\input (\input ));
  not not_1 (not_1_out[1], not_1_out[3]);
  Comparator #(.width(17), .mode("unsigned")) comparator_1 (
    .a({1'b0, stage1_1_input_o}), .b(stage1_1_square1_o), .lt(comparator_1_lt));  // open: gt, eq
  Adder #(.width(5)) adder_1 (
    .a(stage1_1_square1_o[4:0]), .b({root[1:0], 3'b111}), .out(adder_1_out), .cin(1'b1), .cout(adder_1_cout));
  Adder #(.width(4)) adder_2 (
    .a(root[3:0]), .b({{2{not_1_out[3]}}, not_1_out[1], 1'b0}), .out(adder_2_out), .cout(adder_2_cout));  // open: cin
  STAGE2 stage2_1 (
    .square_sum(adder_1_out), .Co(adder_1_cout), .A_high(stage1_1_square1_o[16:5]),
    .B_high({{6{1'b0}}, root[7:2]}), .square_sum_o(stage2_1_square_sum_o), .Co_o(stage2_1_co_o),
    .A_high_o(stage2_1_a_high_o), .B_high_o(stage2_1_b_high_o), .en_pipe(controlpath_1_en_pipe), .clk(clk),
    .rst(rst), .N(comparator_1_lt), .N_o(stage2_1_n_o), .root_sum(adder_2_out),
    .root_sum_o(stage2_1_root_sum_o[3:0]), .Co_root(adder_2_cout), .Co_root_o(stage2_1_co_root_o),
    .root_high(root[7:4]), .root_high_o(stage2_1_root_high_o));
  Adder #(.width(4)) adder_3 (
    .a(stage2_1_a_high_o[3:0]), .b(stage2_1_b_high_o[3:0]), .out(adder_3_out), .cin(stage2_1_co_o),
    .cout(adder_3_cout));
  Adder #(.width(4)) adder_4 (
    .a(stage2_1_root_high_o), .b({4{not_1_out[3]}}), .out(stage2_1_root_sum_o[7:4]), .cin(stage2_1_co_root_o));  // open: cout
  STAGE3 stage3_1 (
    .square_sum({adder_3_out, stage2_1_square_sum_o}), .Co(adder_3_cout), .A_high(stage2_1_a_high_o[11:4]),
    .B_high(stage2_1_b_high_o[11:4]), .square_sum_o(stage3_1_square_sum_o), .Co_o(stage3_1_co_o),
    .A_high_o(stage3_1_a_high_o), .B_high_o(stage3_1_b_high_o), .en_pipe(controlpath_1_en_pipe), .clk(clk),
    .rst(rst));  // open: N, N_o
  Adder #(.width(4)) adder_5 (
    .a(stage3_1_a_high_o[3:0]), .b(stage3_1_b_high_o[3:0]), .out(adder_5_out), .cin(stage3_1_co_o),
    .cout(adder_5_cout));
  STAGE4 stage4_1 (
    .ready(controlpath_1_ready), .square_sum({adder_5_out, stage3_1_square_sum_o}), .Co(adder_5_cout),
    .A_high(stage3_1_a_high_o[7:4]), .B_high(stage3_1_b_high_o[7:4]), .ready_o(ready),
    .square_sum_o(stage4_1_square_sum_o), .Co_o(stage4_1_co_o), .A_high_o(stage4_1_a_high_o),
    .B_high_o(stage4_1_b_high_o), .en_pipe(controlpath_1_en_pipe), .clk(clk), .rst(rst));  // open: N, N_o
  Adder #(.width(4)) adder_6 (
    .a(stage4_1_a_high_o), .b(stage4_1_b_high_o), .out(adder_6_out), .cin(stage4_1_co_o));  // open: cout
  Counter #(.width(10), .max('h3ff)) counter_1 (
    .count(ready), .Q(counter_1_q), .clk(clk), .clr(rst));  // open: load, D, carry
  // Probe on counter_1_q
  // Probe on root

  // Notes on the sheet:
  //   root<<3 + 7
  //   2 or -6
  //   0 or -1
  //   Cycles
endmodule

module STAGE1 (
  input  [15:0] \input ,
  input  [16:0] square1,
  input  [7:0] root,
  input  wr_input,
  input  en_pipe,
  input  clk,
  input  rst,
  output [15:0] input_o,
  output [16:0] square1_o,
  output [7:0] root_o
);

  Register #(.width(16)) u_input (.D(\input ), .en(wr_input), .Q(input_o), .clk(clk), .clr(rst));
  Register #(.width(17)) u_square1 (.D(square1), .en(en_pipe), .Q(square1_o), .clk(clk), .clr(rst));
  reg_root_S1 reg_root_s1_1 (.square_sum(root), .en(en_pipe), .square_sum_o(root_o), .clk(clk), .rst(rst));
endmodule

module STAGE2 (
  input  N,
  input  [4:0] square_sum,
  input  Co,
  input  [11:0] A_high,
  input  [11:0] B_high,
  input  [3:0] root_sum,
  input  Co_root,
  input  [3:0] root_high,
  input  en_pipe,
  input  clk,
  input  rst,
  output N_o,
  output [4:0] square_sum_o,
  output Co_o,
  output [11:0] A_high_o,
  output [11:0] B_high_o,
  output [3:0] root_sum_o,
  output Co_root_o,
  output [3:0] root_high_o
);

  Register #(.width(1)) u_N (.D(N), .en(en_pipe), .Q(N_o), .clk(clk), .clr(rst));
  reg_square_S2 reg_square_s2_1 (
    .square_sum(square_sum), .en(en_pipe), .square_sum_o(square_sum_o), .clk(clk), .rst(rst));
  Register #(.width(1)) u_Co (.D(Co), .en(en_pipe), .Q(Co_o), .clk(clk), .clr(rst));
  Register #(.width(12)) u_A_high (.D(A_high), .en(en_pipe), .Q(A_high_o), .clk(clk), .clr(rst));
  Register #(.width(12)) u_B_high (.D(B_high), .en(en_pipe), .Q(B_high_o), .clk(clk), .clr(rst));
  reg_root_S2 reg_root_s2_1 (.root_sum(root_sum), .en(en_pipe), .square_sum_o(root_sum_o), .clk(clk), .rst(rst));
  Register #(.width(1)) Co_2 (.D(Co_root), .en(en_pipe), .Q(Co_root_o), .clk(clk), .clr(rst));
  Register #(.width(4)) u_root_high (.D(root_high), .en(en_pipe), .Q(root_high_o), .clk(clk), .clr(rst));
endmodule

module STAGE3 (
  input  N,
  input  [8:0] square_sum,
  input  Co,
  input  [7:0] A_high,
  input  [7:0] B_high,
  input  en_pipe,
  input  clk,
  input  rst,
  output N_o,
  output [8:0] square_sum_o,
  output Co_o,
  output [7:0] A_high_o,
  output [7:0] B_high_o
);

  Register #(.width(1)) u_N (.D(N), .en(en_pipe), .Q(N_o), .clk(clk), .clr(rst));
  reg_square_S3 reg_square_s3_1 (
    .square_sum(square_sum), .en(en_pipe), .square_sum_o(square_sum_o), .clk(clk), .rst(rst));
  Register #(.width(1)) u_Co (.D(Co), .en(en_pipe), .Q(Co_o), .clk(clk), .clr(rst));
  Register u_A_high (.D(A_high), .en(en_pipe), .Q(A_high_o), .clk(clk), .clr(rst));
  Register u_B_high (.D(B_high), .en(en_pipe), .Q(B_high_o), .clk(clk), .clr(rst));
endmodule

module STAGE4 (
  input  ready,
  input  N,
  input  [12:0] square_sum,
  input  Co,
  input  [3:0] A_high,
  input  [3:0] B_high,
  input  en_pipe,
  input  clk,
  input  rst,
  output ready_o,
  output N_o,
  output [12:0] square_sum_o,
  output Co_o,
  output [3:0] A_high_o,
  output [3:0] B_high_o
);

  D_Flip_Flop d_ff_1 (.clk(clk), .D(ready), .Q(ready_o), .preset(rst), .en(en_pipe));  // open: Qn, reset
  Register #(.width(1)) u_N (.D(N), .en(en_pipe), .Q(N_o), .clk(clk), .clr(rst));
  reg_square_S4 reg_square_s4_1 (
    .square_sum(square_sum), .en(en_pipe), .square_sum_o(square_sum_o), .clk(clk), .rst(rst));
  Register #(.width(1)) u_Co (.D(Co), .en(en_pipe), .Q(Co_o), .clk(clk), .clr(rst));
  Register #(.width(4)) u_A_high (.D(A_high), .en(en_pipe), .Q(A_high_o), .clk(clk), .clr(rst));
  Register #(.width(4)) u_B_high (.D(B_high), .en(en_pipe), .Q(B_high_o), .clk(clk), .clr(rst));
endmodule

module ControlPath (
  input  N,
  input  clk,
  input  rst,
  output wr_input,
  output en_pipe,
  output ready,
  output mux_root
);

  wire nextstage_1_q0_2, nextstage_1_q1_2, nextstage_1_q2_2, Q0_q, Q1_q, Q2_q;

  NextStage nextstage_1 (
    .Q2(Q2_q), .Q1(Q1_q), .Q0(Q0_q), .N(N), .q2_2(nextstage_1_q2_2), .q1_2(nextstage_1_q1_2),
    .q0_2(nextstage_1_q0_2));
  D_Flip_Flop Q2 (.clk(clk), .D(nextstage_1_q2_2), .Q(Q2_q), .reset(rst));  // open: Qn, preset, en
  D_Flip_Flop Q1 (.clk(clk), .D(nextstage_1_q1_2), .Q(Q1_q), .reset(rst));  // open: Qn, preset, en
  D_Flip_Flop Q0 (.clk(clk), .D(nextstage_1_q0_2), .Q(Q0_q), .reset(rst));  // open: Qn, preset, en
  Outputs outputs_1 (
    .Q2(Q2_q), .Q1(Q1_q), .Q0(Q0_q), .wr_input(wr_input), .en_pipe(en_pipe), .ready(ready),
    .mux_root(mux_root));
endmodule

module NextStage (
  input  Q2,
  input  Q1,
  input  Q0,
  input  N,
  output q2_2,
  output q1_2,
  output q0_2
);

  wire and_2_out, not_1_out;

  and and_1 (q2_2, Q1, not_1_out);
  not not_1 (not_1_out, Q0);
  and and_2 (and_2_out, Q0, N);
  not not_2 (q0_2, Q1);
  or or_1 (q1_2, and_2_out, Q1);
endmodule

module Outputs (
  input  Q2,
  input  Q1,
  input  Q0,
  output wr_input,
  output en_pipe,
  output ready,
  output mux_root
);

  wire and_2_out, not_1_out, not_2_out, not_3_out;

  not not_1 (not_1_out, Q1);
  not not_2 (not_2_out, Q0);
  not not_3 (not_3_out, Q2);
  and and_1 (wr_input, not_1_out, not_2_out);
  and and_2 (and_2_out, not_3_out, Q1);
  or or_1 (en_pipe, Q0, and_2_out);

  assign mux_root = Q1;
  assign ready = Q0;
endmodule

module reg_square_S2 (
  input  [4:0] square_sum,
  input  en,
  input  clk,
  input  rst,
  output [4:0] square_sum_o
);

  D_Flip_Flop d_ff_1 (.clk(clk), .D(square_sum[0]), .Q(square_sum_o[0]), .preset(rst), .en(en));  // open: Qn, reset
  D_Flip_Flop d_ff_2 (.clk(clk), .D(square_sum[1]), .Q(square_sum_o[1]), .en(en), .reset(rst));  // open: Qn, preset
  D_Flip_Flop d_ff_3 (.clk(clk), .D(square_sum[2]), .Q(square_sum_o[2]), .en(en), .reset(rst));  // open: Qn, preset
  D_Flip_Flop d_ff_4 (.clk(clk), .D(square_sum[3]), .Q(square_sum_o[3]), .preset(rst), .en(en));  // open: Qn, reset
  D_Flip_Flop d_ff_5 (.clk(clk), .D(square_sum[4]), .Q(square_sum_o[4]), .en(en), .reset(rst));  // open: Qn, preset
endmodule

module reg_square_S3 (
  input  [8:0] square_sum,
  input  en,
  input  clk,
  input  rst,
  output [8:0] square_sum_o
);

  Register #(.width(2)) register_1 (.D(square_sum[1:0]), .en(en), .Q(square_sum_o[1:0]), .clk(clk), .clr(rst));
  D_Flip_Flop d_ff_1 (.clk(clk), .D(square_sum[2]), .Q(square_sum_o[2]), .preset(rst), .en(en));  // open: Qn, reset
  Register #(.width(6)) register_2 (.D(square_sum[8:3]), .en(en), .Q(square_sum_o[8:3]), .clk(clk), .clr(rst));
endmodule

module reg_square_S4 (
  input  [12:0] square_sum,
  input  en,
  input  clk,
  input  rst,
  output [12:0] square_sum_o
);

  D_Flip_Flop d_ff_1 (.clk(clk), .D(square_sum[0]), .Q(square_sum_o[0]), .preset(rst), .en(en));  // open: Qn, reset
  Register #(.width(12)) register_1 (.D(square_sum[12:1]), .en(en), .Q(square_sum_o[12:1]), .clk(clk), .clr(rst));
endmodule

module reg_root_S1 (
  input  [7:0] square_sum,
  input  en,
  input  clk,
  input  rst,
  output [7:0] square_sum_o
);

  D_Flip_Flop d_ff_1 (.clk(clk), .D(square_sum[0]), .Q(square_sum_o[0]), .preset(rst), .en(en));  // open: Qn, reset
  Register #(.width(7)) register_1 (.D(square_sum[7:1]), .en(en), .Q(square_sum_o[7:1]), .clk(clk), .clr(rst));
endmodule

module reg_root_S2 (
  input  [3:0] root_sum,
  input  en,
  input  clk,
  input  rst,
  output [3:0] square_sum_o
);

  D_Flip_Flop d_ff_1 (.clk(clk), .D(root_sum[0]), .Q(square_sum_o[0]), .en(en), .reset(rst));  // open: Qn, preset
  D_Flip_Flop d_ff_2 (.clk(clk), .D(root_sum[1]), .Q(square_sum_o[1]), .preset(rst), .en(en));  // open: Qn, reset
  Register #(.width(2)) register_1 (.D(root_sum[3:2]), .en(en), .Q(square_sum_o[3:2]), .clk(clk), .clr(rst));
endmodule

module f (
  input  N,
  output A,
  output B,
  output C,
  output D
);


  assign A = N;
  assign B = 1'b0;
  assign C = 1'b1;
  assign D = 1'b0;
endmodule
