// Logisim project BubbleSort.circ as structural Verilog: 4 circuits, main circuit main
module main (
);

  wire and_1_out, clk, comparator_1_eq, comparator_2_lt, comparator_3_eq, comparator_4_eq,
       controlpath_1_en_counter, controlpath_1_en_sr, controlpath_1_mux_in, controlpath_1_rst_cntr,
       controlpath_1_wr_bigger, controlpath_1_wr_last, nor_1_out, not_1_out, or_1_out, ready, rst, serial_on;
  wire [3:0] counter_3_q;
  wire [7:0] counter_1_q, counter_4_q;
  wire [9:0] counter_2_q;
  wire [31:0] First_q, Last_q, multiplexer_1_out, multiplexer_2_out, ram_1_data, register_1_q, register_2_q,
       register_3_q, register_4_q, register_5_q, register_6_q, register_7_q, register_8_q, register_9_q,
       register_10_q;

  not not_1 (not_1_out, ready);
  Clock clock_1 (.out(clk));
  Button button_1 (.out(rst));
  Counter counter_1 (.Q(counter_1_q), .clk(clk), .clr(rst));  // open: load, D, count, carry
  Counter #(.width(10), .max('h3ff)) counter_2 (
    .count(not_1_out), .Q(counter_2_q), .clk(clk), .clr(rst));  // open: load, D, carry
  // Probe on counter_2_q
  ControlPath controlpath_1 (
    .eh_maior(comparator_2_lt), .end_comp(comparator_3_eq), .end_stf(comparator_4_eq),
    .end_count(comparator_1_eq), .clk(clk), .rst(rst), .wr_bigger(controlpath_1_wr_bigger),
    .wr_last(controlpath_1_wr_last), .en_counter(controlpath_1_en_counter), .mux_in(controlpath_1_mux_in),
    .rst_cntr(controlpath_1_rst_cntr), .en_sr(controlpath_1_en_sr), .serial_on(serial_on), .ready(ready));
  RAM #(.dataWidth(32)) ram_1 (.addr(counter_1_q), .data(ram_1_data));  // open: sel, clk, ld, clr
  Multiplexer #(.width(32)) multiplexer_1 (
    .in0(ram_1_data), .in1(multiplexer_2_out), .out(multiplexer_1_out), .sel(controlpath_1_mux_in));  // open: en
  Counter #(.width(4), .max('hf)) counter_3 (
    .count(controlpath_1_en_counter), .Q(counter_3_q), .clk(clk), .clr(or_1_out));  // open: load, D, carry
  or or_1 (or_1_out, controlpath_1_rst_cntr, rst);
  Register #(.width(32)) register_1 (
    .D(multiplexer_1_out), .en(controlpath_1_en_sr), .Q(register_1_q), .clk(clk), .clr(rst));
  Comparator #(.width(4)) comparator_1 (.a(4'b1001), .b(counter_3_q), .eq(comparator_1_eq));  // open: gt, lt
  Register #(.width(32)) register_2 (
    .D(register_1_q), .en(controlpath_1_en_sr), .Q(register_2_q), .clk(clk), .clr(rst));
  Register #(.width(32)) register_3 (
    .D(register_2_q), .en(controlpath_1_en_sr), .Q(register_3_q), .clk(clk), .clr(rst));
  nor nor_1 (nor_1_out, counter_3_q[0], counter_3_q[1], counter_3_q[2], counter_3_q[3]);
  Register #(.width(32)) register_4 (
    .D(register_3_q), .en(controlpath_1_en_sr), .Q(register_4_q), .clk(clk), .clr(rst));
  Register #(.width(32)) register_5 (
    .D(register_4_q), .en(controlpath_1_en_sr), .Q(register_5_q), .clk(clk), .clr(rst));
  Register #(.width(32)) register_6 (
    .D(register_5_q), .en(controlpath_1_en_sr), .Q(register_6_q), .clk(clk), .clr(rst));
  Register #(.width(32)) register_7 (
    .D(register_6_q), .en(controlpath_1_en_sr), .Q(register_7_q), .clk(clk), .clr(rst));
  Multiplexer #(.width(32)) multiplexer_2 (
    .in0(register_8_q), .in1(register_10_q), .out(multiplexer_2_out), .sel(controlpath_1_wr_bigger));  // open: en
  Register #(.width(32)) register_8 (
    .D(register_9_q), .en(controlpath_1_en_sr), .Q(register_8_q), .clk(clk), .clr(rst));
  Register #(.width(32)) register_9 (
    .D(register_7_q), .en(controlpath_1_en_sr), .Q(register_9_q), .clk(clk), .clr(rst));
  Register #(.width(32)) Last (.D(multiplexer_2_out), .en(controlpath_1_wr_last), .Q(Last_q), .clk(clk), .clr(rst));
  Register #(.width(32)) First (.D(register_10_q), .en(nor_1_out), .Q(First_q), .clk(clk), .clr(rst));
  and and_1 (and_1_out, serial_on, ~ready);  // AND_Gate
  Register #(.width(32)) register_10 (
    .D(register_8_q), .en(controlpath_1_wr_bigger), .Q(register_10_q), .clk(clk), .clr(rst));
  Counter counter_4 (.count(and_1_out), .Q(counter_4_q), .clk(clk), .clr(rst));  // open: load, D, carry
  Comparator #(.width(32)) comparator_2 (.a(register_10_q), .b(register_8_q), .lt(comparator_2_lt));  // open: gt, eq
  Comparator #(.width(32)) comparator_3 (.a(register_8_q), .b(Last_q), .eq(comparator_3_eq));  // open: gt, lt
  Comparator #(.width(32)) comparator_4 (.a(register_10_q), .b(First_q), .eq(comparator_4_eq));  // open: gt, lt
  RAM #(.dataWidth(32)) ram_2 (.addr(counter_4_q), .data(register_10_q), .clk(clk), .ld(1'b0), .clr(rst));  // open: sel
endmodule

module NextState (
  input  Q2,
  input  Q1,
  input  Q0,
  input  eh_maior,
  input  end_comp,
  input  end_sft,
  input  end_count,
  output q2_2,
  output q1_2,
  output q0_2
);

  wire and_1_out, and_2_out, and_3_out, and_4_out, and_5_out, and_6_out, and_7_out, and_8_out, and_9_out,
       and_10_out, not_1_out, not_2_out, not_3_out, not_4_out, not_5_out, not_6_out, not_7_out, not_8_out,
       not_9_out, not_10_out, not_11_out;

  not not_1 (not_1_out, Q0);
  not not_2 (not_2_out, end_sft);
  not not_3 (not_3_out, Q1);
  not not_4 (not_4_out, end_sft);
  not not_5 (not_5_out, Q2);
  not not_6 (not_6_out, end_count);
  not not_7 (not_7_out, Q2);
  not not_8 (not_8_out, Q1);
  not not_9 (not_9_out, Q2);
  not not_10 (not_10_out, end_sft);
  not not_11 (not_11_out, end_count);
  and and_1 (and_1_out, Q1, not_1_out);
  and and_2 (and_2_out, Q1, end_comp, not_2_out);
  and and_3 (and_3_out, Q2, not_3_out);
  and and_4 (and_4_out, Q2, not_4_out);
  and and_5 (and_5_out, not_5_out, Q1);
  and and_6 (and_6_out, Q1, not_6_out);
  and and_7 (and_7_out, not_7_out, not_8_out, end_count);
  and and_8 (and_8_out, not_9_out, Q0);
  and and_9 (and_9_out, Q0, not_10_out);
  and and_10 (and_10_out, Q0, not_11_out);
  or or_1 (q2_2, and_1_out, and_2_out, and_3_out, and_4_out);
  or or_2 (q1_2, Q0, and_5_out, and_6_out);
  or or_3 (q0_2, and_7_out, and_8_out, and_9_out, and_10_out);
endmodule

module outputs (
  input  Q2,
  input  Q1,
  input  Q0,
  input  eh_maior,
  input  end_comp,
  input  end_sft,
  input  end_count,
  output wr_bigger,
  output wr_last,
  output en_counter,
  output mux_in,
  output rst_cntr,
  output en_sr,
  output serial_on,
  output ready
);

  wire and_1_out, and_2_out, and_3_out, and_4_out, and_5_out, and_6_out, and_7_out, and_8_out, and_9_out,
       and_10_out, and_11_out, and_12_out, and_13_out, and_14_out, not_1_out, not_2_out, not_3_out,
       not_4_out, not_5_out, not_6_out, not_7_out, not_8_out, not_9_out, not_10_out, not_11_out, not_12_out,
       not_13_out, not_14_out, not_15_out, not_16_out, not_17_out, not_18_out;

  not not_1 (not_1_out, Q2);
  not not_2 (not_2_out, Q1);
  not not_3 (not_3_out, Q0);
  not not_4 (not_4_out, Q1);
  not not_5 (not_5_out, Q2);
  not not_6 (not_6_out, Q2);
  not not_7 (not_7_out, Q1);
  not not_8 (not_8_out, Q0);
  not not_9 (not_9_out, Q2);
  not not_10 (not_10_out, Q0);
  or or_1 (mux_in, Q0, Q1);
  not not_11 (not_11_out, Q1);
  not not_12 (not_12_out, Q2);
  not not_13 (not_13_out, Q0);
  not not_14 (not_14_out, Q2);
  not not_15 (not_15_out, Q1);
  not not_16 (not_16_out, Q2);
  not not_17 (not_17_out, Q0);
  not not_18 (not_18_out, Q1);
  and and_1 (and_1_out, not_1_out, not_2_out, not_3_out);
  and and_2 (and_2_out, Q0, eh_maior);
  and and_3 (and_3_out, Q1, Q0, end_comp);
  and and_4 (and_4_out, Q2, Q1);
  and and_5 (and_5_out, not_4_out, Q0);
  and and_6 (and_6_out, not_5_out, Q0, end_comp);
  and and_7 (and_7_out, not_6_out, not_7_out, not_8_out);
  and and_8 (and_8_out, not_9_out, Q1, Q0, end_comp);
  and and_9 (and_9_out, Q2, Q1, not_10_out);
  and and_10 (and_10_out, not_11_out, Q0);
  and and_11 (and_11_out, not_12_out, Q1, not_13_out);
  and and_12 (and_12_out, not_14_out, not_15_out);
  and and_13 (and_13_out, not_16_out, Q0);
  and and_14 (and_14_out, Q2, Q1);
  and and_15 (serial_on, Q2, not_17_out);
  and and_16 (ready, Q2, not_18_out);
  or or_2 (wr_bigger, and_1_out, and_2_out, and_3_out, and_4_out);
  or or_3 (wr_last, and_5_out, and_6_out);
  or or_4 (en_counter, and_7_out, and_8_out, and_9_out);
  or or_5 (rst_cntr, and_10_out, and_11_out);
  or or_6 (en_sr, and_12_out, and_13_out, and_14_out);
endmodule

module ControlPath (
  input  eh_maior,
  input  end_comp,
  input  end_stf,
  input  end_count,
  input  clk,
  input  rst,
  output wr_bigger,
  output wr_last,
  output en_counter,
  output mux_in,
  output rst_cntr,
  output en_sr,
  output serial_on,
  output ready
);

  wire nextstate_1_q0_2, nextstate_1_q1_2, nextstate_1_q2_2, Q0_q, Q1_q, Q2_q;

  NextState nextstate_1 (
    .Q2(Q2_q), .Q1(Q1_q), .Q0(Q0_q), .eh_maior(eh_maior), .end_comp(end_comp), .end_sft(end_stf),
    .end_count(end_count), .q2_2(nextstate_1_q2_2), .q1_2(nextstate_1_q1_2), .q0_2(nextstate_1_q0_2));
  D_Flip_Flop Q2 (.clk(clk), .D(nextstate_1_q2_2), .Q(Q2_q), .reset(rst));  // open: Qn, preset, en
  D_Flip_Flop Q1 (.clk(clk), .D(nextstate_1_q1_2), .Q(Q1_q), .reset(rst));  // open: Qn, preset, en
  D_Flip_Flop Q0 (.clk(clk), .D(nextstate_1_q0_2), .Q(Q0_q), .reset(rst));  // open: Qn, preset, en
  outputs outputs_1 (
    .Q2(Q2_q), .Q1(Q1_q), .Q0(Q0_q), .eh_maior(eh_maior), .end_comp(end_comp), .end_sft(end_stf),
    .end_count(end_count), .wr_bigger(wr_bigger), .wr_last(wr_last), .en_counter(en_counter),
    .mux_in(mux_in), .rst_cntr(rst_cntr), .en_sr(en_sr), .serial_on(serial_on), .ready(ready));
endmodule
