// Logisim project SquareRoot_Pipeline_V1.2.circ as structural Verilog: 6 circuits, main circuit Pipeline
module NextStage (
  input  Q2,
  input  Q1,
  input  Q0,
  input  N,
  output q2_2,
  output q1_2,
  output q0_2
);

  wire and_1_out, and_2_out, and_3_out, not_1_out, not_2_out, not_3_out, not_4_out;

  and and_1 (and_1_out, Q0, N);
  not not_1 (not_1_out, Q2);
  or or_1 (q1_2, not_1_out, Q0);
  not not_2 (not_2_out, Q2);
  and and_2 (and_2_out, not_2_out, Q1, not_3_out);
  not not_3 (not_3_out, Q0);
  not not_4 (not_4_out, Q2);
  and and_3 (and_3_out, not_4_out, Q1, N);
  or or_2 (q2_2, and_1_out, Q2);
  or or_3 (q0_2, and_2_out, and_3_out);
endmodule

module Outputs (
  input  Q2,
  input  Q1,
  input  Q0,
  output boot,
  output wr_root,
  output wr_square,
  output en_pipe,
  output ready,
  output mux_root,
  output mux_square
);

  wire and_2_out, and_3_out, not_1_out, not_2_out, not_3_out, not_4_out, not_5_out, not_6_out, not_7_out,
       not_9_out;

  not not_1 (not_1_out, Q2);
  not not_2 (not_2_out, Q1);
  not not_3 (not_3_out, Q2);
  not not_4 (not_4_out, Q0);
  not not_5 (not_5_out, Q2);
  not not_6 (not_6_out, Q0);
  not not_7 (not_7_out, Q2);
  not not_8 (ready, Q2);
  not not_9 (not_9_out, Q0);
  and and_1 (boot, not_1_out, not_2_out);
  and and_2 (and_2_out, not_3_out, not_4_out);
  and and_3 (and_3_out, Q2, Q0);
  and and_4 (wr_square, not_5_out, not_6_out);
  or or_1 (en_pipe, not_7_out, Q1);
  and and_5 (mux_square, Q1, not_9_out);
  or or_2 (wr_root, and_2_out, and_3_out);

  assign mux_root = Q2;
endmodule

module ControlPath (
  input  N,
  input  clk,
  input  rst,
  output boot,
  output wr_root,
  output wr_square,
  output en_pipe,
  output ready,
  output mux_root,
  output mux_square
);

  wire nextstage_1_q0_2, nextstage_1_q1_2, nextstage_1_q2_2, Q0_q, Q1_q, Q2_q;

  NextStage nextstage_1 (
    .Q2(Q2_q), .Q1(Q1_q), .Q0(Q0_q), .N(N), .q2_2(nextstage_1_q2_2), .q1_2(nextstage_1_q1_2),
    .q0_2(nextstage_1_q0_2));
  D_Flip_Flop Q2 (.clk(clk), .D(nextstage_1_q2_2), .Q(Q2_q), .reset(rst));  // open: Qn, preset, en
  D_Flip_Flop Q1 (.clk(clk), .D(nextstage_1_q1_2), .Q(Q1_q), .reset(rst));  // open: Qn, preset, en
  D_Flip_Flop Q0 (.clk(clk), .D(nextstage_1_q0_2), .Q(Q0_q), .reset(rst));  // open: Qn, preset, en
  Outputs outputs_1 (
    .Q2(Q2_q), .Q1(Q1_q), .Q0(Q0_q), .boot(boot), .wr_root(wr_root), .wr_square(wr_square),
    .en_pipe(en_pipe), .ready(ready), .mux_root(mux_root), .mux_square(mux_square));
endmodule

module Pipeline (
  input  [15:0] \input ,
  input  [15:0] square_init,
  input  [7:0] root_init,
  output ready,
  output [7:0] root
);

  wire adder_1_cout, clk, controlpath_1_boot, controlpath_1_en_pipe, controlpath_1_mux_root,
       controlpath_1_mux_square, controlpath_1_ready, controlpath_1_wr_root, controlpath_1_wr_square, rst,
       stage1_1_mux_root_o, stage1_1_mux_square_o, stage1_1_ready_o, stage1_1_wr_root_s_o,
       stage1_1_wr_square_s_o, stage2_1_co_o, stage2_1_wr_root_s_o, stage2_1_wr_square_s_o;
  wire [7:0] adder_1_out, adder_2_out, multiplexer_2_out, multiplexer_5_out, stage1_1_root_o;
  wire [8:0] stage2_1_a_high_o, stage2_1_b_high_o;
  wire [9:0] counter_1_q;
  wire [15:0] stage1_1_input_o;
  wire [16:0] multiplexer_1_out, multiplexer_3_out, multiplexer_4_out, not_1_out, shifter_1_out,
       stage1_1_square_o, stage2_1_sum_low_o;

  // Probe on \input 
  Clock u_clk (.out(clk));
  Button button_1 (.out(rst));
  ControlPath controlpath_1 (
    .N(stage2_1_sum_low_o[16]), .clk(clk), .rst(rst), .en_pipe(controlpath_1_en_pipe),
    .wr_square(controlpath_1_wr_square), .wr_root(controlpath_1_wr_root), .boot(controlpath_1_boot),
    .ready(controlpath_1_ready), .mux_root(controlpath_1_mux_root), .mux_square(controlpath_1_mux_square));
  Multiplexer #(.width(17)) multiplexer_1 (
    .in0(stage2_1_sum_low_o), .in1({1'b0, square_init}), .out(multiplexer_1_out), .sel(controlpath_1_boot));  // open: en
  Multiplexer #(.width(8)) multiplexer_2 (
    .in0(root), .in1(root_init), .out(multiplexer_2_out), .sel(controlpath_1_boot));  // open: en
  STAGE1 stage1_1 (
    .wr_root_s(controlpath_1_wr_root), .wr_square_s(controlpath_1_wr_square),
    .mux_root(controlpath_1_mux_root), .mux_square(controlpath_1_mux_square), .\input (\input ),
    .square(multiplexer_1_out), .root(multiplexer_2_out), .wr_root_s_o(stage1_1_wr_root_s_o),
    .wr_square_s_o(stage1_1_wr_square_s_o), .mux_root_o(stage1_1_mux_root_o),
    .mux_square_o(stage1_1_mux_square_o), .input_o(stage1_1_input_o), .square_o(stage1_1_square_o),
    .root_o(stage1_1_root_o), .en_pipe(controlpath_1_en_pipe), .boot(controlpath_1_boot),
    .wr_square(stage2_1_wr_square_s_o), .wr_root(stage2_1_wr_root_s_o), .clk(clk), .rst(rst),
    .ready(controlpath_1_ready), .ready_o(stage1_1_ready_o));
  assign not_1_out = ~stage1_1_square_o;  // NOT_Gate not_1, 17 bits wide
  Shifter #(.width(17)) shifter_1 (.in({{9{1'b0}}, stage1_1_root_o}), .\dist (5'b00001), .out(shifter_1_out));
  Multiplexer #(.width(17)) multiplexer_3 (
    .in0({1'b0, stage1_1_input_o}), .in1(stage1_1_square_o), .out(multiplexer_3_out),
    .sel(stage1_1_mux_square_o));  // open: en
  Multiplexer #(.width(17)) multiplexer_4 (
    .in0(not_1_out), .in1(shifter_1_out), .out(multiplexer_4_out), .sel(stage1_1_mux_square_o));  // open: en
  Multiplexer #(.width(8)) multiplexer_5 (
    .in0(8'h1), .in1(8'hfd), .out(multiplexer_5_out), .sel(stage1_1_mux_root_o));  // open: en
  Adder adder_1 (
    .a(multiplexer_3_out[7:0]), .b(multiplexer_4_out[7:0]), .out(adder_1_out), .cin(1'b1), .cout(adder_1_cout));
  Adder adder_2 (.a(multiplexer_5_out), .b(stage1_1_root_o), .out(adder_2_out));  // open: cin, cout
  STAGE2 stage2_1 (
    .ready(stage1_1_ready_o), .wr_root_s(stage1_1_wr_root_s_o), .wr_square_s(stage1_1_wr_square_s_o),
    .Sum_low(adder_1_out), .Co(adder_1_cout), .A_high(multiplexer_3_out[16:8]),
    .B_high(multiplexer_4_out[16:8]), .root(adder_2_out), .ready_o(ready),
    .wr_root_s_o(stage2_1_wr_root_s_o), .wr_square_s_o(stage2_1_wr_square_s_o),
    .Sum_low_o(stage2_1_sum_low_o[7:0]), .Co_o(stage2_1_co_o), .A_high_o(stage2_1_a_high_o),
    .B_high_o(stage2_1_b_high_o), .root_o(root), .en_pipe(controlpath_1_en_pipe), .clk(clk), .rst(rst));
  Adder #(.width(9)) adder_3 (
    .a(stage2_1_a_high_o), .b(stage2_1_b_high_o), .out(stage2_1_sum_low_o[16:8]), .cin(stage2_1_co_o));  // open: cout
  // Probe on root
  Counter #(.width(10), .max('h3ff)) counter_1 (
    .count(ready), .Q(counter_1_q), .clk(clk), .clr(rst));  // open: load, D, carry
  // Probe on counter_1_q
endmodule

module STAGE1 (
  input  ready,
  input  wr_root_s,
  input  wr_square_s,
  input  mux_root,
  input  mux_square,
  input  [15:0] \input ,
  input  [16:0] square,
  input  [7:0] root,
  input  en_pipe,
  input  boot,
  input  wr_square,
  input  wr_root,
  input  clk,
  input  rst,
  output ready_o,
  output wr_root_s_o,
  output wr_square_s_o,
  output mux_root_o,
  output mux_square_o,
  output [15:0] input_o,
  output [16:0] square_o,
  output [7:0] root_o
);

  D_Flip_Flop d_ff_1 (.clk(clk), .D(ready), .Q(ready_o), .preset(rst), .en(en_pipe));  // open: Qn, reset
  Register #(.width(1)) u_wr_root (.D(wr_root_s), .en(en_pipe), .Q(wr_root_s_o), .clk(clk), .clr(rst));
  Register #(.width(1)) u_wr_square (.D(wr_square_s), .en(en_pipe), .Q(wr_square_s_o), .clk(clk), .clr(rst));
  Register #(.width(1)) u_mux_root (.D(mux_root), .en(en_pipe), .Q(mux_root_o), .clk(clk), .clr(rst));
  Register #(.width(1)) u_mux_square (.D(mux_square), .en(en_pipe), .Q(mux_square_o), .clk(clk), .clr(rst));
  Register #(.width(16)) u_Input (.D(\input ), .en(boot), .Q(input_o), .clk(clk), .clr(rst));
  Register #(.width(17)) u_square (.D(square), .en(wr_square), .Q(square_o), .clk(clk), .clr(rst));
  Register u_root (.D(root), .en(wr_root), .Q(root_o), .clk(clk), .clr(rst));
endmodule

module STAGE2 (
  input  ready,
  input  wr_root_s,
  input  wr_square_s,
  input  [7:0] Sum_low,
  input  Co,
  input  [8:0] A_high,
  input  [8:0] B_high,
  input  [7:0] root,
  input  en_pipe,
  input  clk,
  input  rst,
  output ready_o,
  output wr_root_s_o,
  output wr_square_s_o,
  output [7:0] Sum_low_o,
  output Co_o,
  output [8:0] A_high_o,
  output [8:0] B_high_o,
  output [7:0] root_o
);

  D_Flip_Flop d_ff_1 (.clk(clk), .D(ready), .Q(ready_o), .preset(rst), .en(en_pipe));  // open: Qn, reset
  Register #(.width(1)) wr_root (.D(wr_root_s), .en(en_pipe), .Q(wr_root_s_o), .clk(clk), .clr(rst));
  Register #(.width(1)) wr_square (.D(wr_square_s), .en(en_pipe), .Q(wr_square_s_o), .clk(clk), .clr(rst));
  Register u_Sum_low (.D(Sum_low), .en(en_pipe), .Q(Sum_low_o), .clk(clk), .clr(rst));
  Register #(.width(1)) u_Co (.D(Co), .en(en_pipe), .Q(Co_o), .clk(clk), .clr(rst));
  Register #(.width(9)) u_A_high (.D(A_high), .en(en_pipe), .Q(A_high_o), .clk(clk), .clr(rst));
  Register #(.width(9)) u_B_high (.D(B_high), .en(en_pipe), .Q(B_high_o), .clk(clk), .clr(rst));
  Register u_root (.D(root), .en(en_pipe), .Q(root_o), .clk(clk), .clr(rst));
endmodule
