// Logisim project SquareRoot_Pipeline_V2.0.circ as structural Verilog: 8 circuits, main circuit Pipeline
module Pipeline (
  input  [15:0] \input ,
  output ready,
  output [7:0] root
);

  wire adder_1_cout, clk, comparator_1_lt, controlpath_1_en_pipe, controlpath_1_ready,
       controlpath_1_wr_input, controlpath_1_wr_square, rst, stage1_1_wr_square_s_o, stage2_1_co_o,
       stage2_1_n_o, stage2_1_wr_square_s_o;
  wire [7:0] adder_1_out, adder_2_out;
  wire [7:7] controlpath_1_mux_root;
  wire [8:0] stage2_1_a_high_o, stage2_1_b_high_o;
  wire [9:0] counter_1_q;
  wire [15:0] stage1_1_input_o;
  wire [16:0] multiplexer_1_out, stage1_1_square1_o, stage1_1_square2_o, stage2_1_sum_low_o;

  Clock clock (.out(clk));
  Button reset (.out(rst));
  // Probe on \input 
  ControlPath controlpath_1 (
    .N(stage2_1_n_o), .clk(clk), .rst(rst), .en_pipe(controlpath_1_en_pipe),
    .wr_square(controlpath_1_wr_square), .wr_input(controlpath_1_wr_input), .ready(controlpath_1_ready),
    .mux_root(controlpath_1_mux_root[7]));
  STAGE1 stage1_1 (
    .wr_square_s(controlpath_1_wr_square), .square2(stage2_1_sum_low_o), .root(adder_2_out),
    .wr_square_s_o(stage1_1_wr_square_s_o), .input_o(stage1_1_input_o), .square2_o(stage1_1_square2_o),
    .root_o(root), .en_pipe(controlpath_1_en_pipe), .wr_input(controlpath_1_wr_input),
    .wr_square(stage2_1_wr_square_s_o), .clk(clk), .rst(rst), .square1(stage2_1_sum_low_o),
    .square1_o(stage1_1_square1_o), .\input (\input ));
  Multiplexer #(.width(17)) multiplexer_1 (
    .in0(stage1_1_square1_o), .in1(stage1_1_square2_o), .out(multiplexer_1_out), .sel(stage1_1_wr_square_s_o));  // open: en
  Comparator #(.width(17), .mode("unsigned")) comparator_1 (
    .a({1'b0, stage1_1_input_o}), .b(multiplexer_1_out), .lt(comparator_1_lt));  // open: gt, eq
  Adder adder_1 (
    .a(multiplexer_1_out[7:0]), .b({root[5:0], 2'b11}), .out(adder_1_out), .cin(1'b1), .cout(adder_1_cout));
  Adder adder_2 (.a({{6{controlpath_1_mux_root[7]}}, 2'b01}), .b(root), .out(adder_2_out));  // open: cin, cout
  STAGE2 stage2_1 (
    .ready(controlpath_1_ready), .wr_square_s(stage1_1_wr_square_s_o), .Sum_low(adder_1_out),
    .Co(adder_1_cout), .A_high(multiplexer_1_out[16:8]), .B_high({{7{1'b0}}, root[7:6]}), .ready_o(ready),
    .wr_square_s_o(stage2_1_wr_square_s_o), .Sum_low_o(stage2_1_sum_low_o[7:0]), .Co_o(stage2_1_co_o),
    .A_high_o(stage2_1_a_high_o), .B_high_o(stage2_1_b_high_o), .en_pipe(controlpath_1_en_pipe), .clk(clk),
    .rst(rst), .N(comparator_1_lt), .N_o(stage2_1_n_o));
  Adder #(.width(9)) adder_3 (
    .a(stage2_1_a_high_o), .b(stage2_1_b_high_o), .out(stage2_1_sum_low_o[16:8]), .cin(stage2_1_co_o));  // open: cout
  // Probe on counter_1_q
  Counter #(.width(10), .max('h3ff)) counter_1 (
    .count(ready), .Q(counter_1_q), .clk(clk), .clr(rst));  // open: load, D, carry
  // Probe on root

  // Notes on the sheet:
  //   root<<2 + 3
endmodule

module STAGE1 (
  input  wr_square_s,
  input  [15:0] \input ,
  input  [16:0] square1,
  input  [16:0] square2,
  input  [7:0] root,
  input  en_pipe,
  input  wr_input,
  input  wr_square,
  input  clk,
  input  rst,
  output wr_square_s_o,
  output [15:0] input_o,
  output [16:0] square1_o,
  output [16:0] square2_o,
  output [7:0] root_o
);

  wire not_1_out;

  not not_1 (not_1_out, wr_square);
  Register #(.width(1)) u_wr_square (.D(wr_square_s), .en(en_pipe), .Q(wr_square_s_o), .clk(clk), .clr(rst));
  Register #(.width(16)) u_input (.D(\input ), .en(wr_input), .Q(input_o), .clk(clk), .clr(rst));
  Register #(.width(17)) u_square1 (.D(square1), .en(not_1_out), .Q(square1_o), .clk(clk), .clr(rst));
  reg_square2 reg_square2_1 (.D(square2), .En(wr_square), .out_5(square2_o), .Clk(clk), .Reset(rst));
  Register u_root (.D(root), .en(en_pipe), .Q(root_o), .clk(clk), .clr(rst));

  // Notes on the sheet:
  //   square2
endmodule

module STAGE2 (
  input  ready,
  input  wr_square_s,
  input  N,
  input  [7:0] Sum_low,
  input  Co,
  input  [8:0] A_high,
  input  [8:0] B_high,
  input  en_pipe,
  input  clk,
  input  rst,
  output ready_o,
  output wr_square_s_o,
  output N_o,
  output [7:0] Sum_low_o,
  output Co_o,
  output [8:0] A_high_o,
  output [8:0] B_high_o
);

  D_Flip_Flop d_ff_1 (.clk(clk), .D(ready), .Q(ready_o), .preset(rst), .en(en_pipe));  // open: Qn, reset
  Register #(.width(1)) wr_square (.D(wr_square_s), .en(en_pipe), .Q(wr_square_s_o), .clk(clk), .clr(rst));
  Register #(.width(1)) u_N (.D(N), .en(en_pipe), .Q(N_o), .clk(clk), .clr(rst));
  Register u_Sum_low (.D(Sum_low), .en(en_pipe), .Q(Sum_low_o), .clk(clk), .clr(rst));
  Register #(.width(1)) u_Co (.D(Co), .en(en_pipe), .Q(Co_o), .clk(clk), .clr(rst));
  Register #(.width(9)) u_A_high (.D(A_high), .en(en_pipe), .Q(A_high_o), .clk(clk), .clr(rst));
  Register #(.width(9)) u_B_high (.D(B_high), .en(en_pipe), .Q(B_high_o), .clk(clk), .clr(rst));
endmodule

module reg_square2 (
  input  [16:0] D,
  input  En,
  input  Clk,
  input  Reset,
  output [16:0] out_5
);

  D_Flip_Flop d_ff_1 (.clk(Clk), .D(D[0]), .Q(out_5[0]), .preset(Reset), .en(En));  // open: Qn, reset
  Register #(.width(16)) register_1 (.D(D[16:1]), .en(En), .Q(out_5[16:1]), .clk(Clk), .clr(Reset));
endmodule

module ControlPath (
  input  N,
  input  clk,
  input  rst,
  output wr_input,
  output wr_square,
  output en_pipe,
  output ready,
  output mux_root
);

  wire nextstage_1_q0_2, nextstage_1_q1_2, nextstage_1_q2_2, Q0_q, Q1_q, Q2_q;

  NextStage nextstage_1 (
    .Q2(Q2_q), .Q1(Q1_q), .Q0(Q0_q), .N(N), .q2_2(nextstage_1_q2_2), .q1_2(nextstage_1_q1_2),
    .q0_2(nextstage_1_q0_2));
  D_Flip_Flop Q2 (.clk(clk), .D(nextstage_1_q2_2), .Q(Q2_q), .reset(rst));  // open: Qn, preset, en
  D_Flip_Flop Q1 (.clk(clk), .D(nextstage_1_q1_2), .Q(Q1_q), .reset(rst));  // open: Qn, preset, en
  D_Flip_Flop Q0 (.clk(clk), .D(nextstage_1_q0_2), .Q(Q0_q), .reset(rst));  // open: Qn, preset, en
  Outputs outputs_1 (
    .Q2(Q2_q), .Q1(Q1_q), .Q0(Q0_q), .wr_input(wr_input), .wr_square(wr_square), .en_pipe(en_pipe),
    .ready(ready), .mux_root(mux_root));
endmodule

module NextStage (
  input  Q2,
  input  Q1,
  input  Q0,
  input  N,
  output q2_2,
  output q1_2,
  output q0_2
);

  wire and_2_out, and_3_out, and_4_out, and_5_out, and_6_out, not_1_out, not_2_out, not_3_out, not_4_out,
       not_5_out, not_6_out;

  and and_1 (q2_2, Q1, not_1_out);
  not not_1 (not_1_out, Q0);
  not not_2 (not_2_out, Q1);
  and and_2 (and_2_out, not_2_out, Q0);
  and and_3 (and_3_out, Q1, not_3_out);
  not not_3 (not_3_out, Q0);
  and and_4 (and_4_out, Q1, N);
  not not_4 (not_4_out, Q1);
  and and_5 (and_5_out, not_4_out, not_5_out);
  not not_5 (not_5_out, Q0);
  and and_6 (and_6_out, Q0, not_6_out);
  not not_6 (not_6_out, N);
  or or_1 (q1_2, and_2_out, and_3_out, and_4_out);
  or or_2 (q0_2, and_5_out, and_6_out);
endmodule

module Outputs (
  input  Q2,
  input  Q1,
  input  Q0,
  output wr_input,
  output wr_square,
  output en_pipe,
  output ready,
  output mux_root
);

  wire and_2_out, not_1_out, not_2_out, not_4_out;

  not not_1 (not_1_out, Q1);
  not not_2 (not_2_out, Q0);
  not not_3 (wr_square, Q1);
  not not_4 (not_4_out, Q2);
  not not_5 (mux_root, Q0);
  and and_1 (wr_input, not_1_out, not_2_out);
  and and_2 (and_2_out, not_4_out, Q1);
  or or_1 (en_pipe, Q0, and_2_out);

  assign ready = Q0;
endmodule

module g (
  input  Flag,
  output S7,
  output S6,
  output S5,
  output S4,
  output S3,
  output S2,
  output S1,
  output S0
);


  assign S0 = 1'b1;
  assign S1 = 1'b0;
  assign S2 = Flag;
  assign S3 = Flag;
  assign S4 = Flag;
  assign S5 = Flag;
  assign S6 = Flag;
  assign S7 = Flag;
endmodule
